# Fritzing sketch ultrasonic (saved by Fritzing 0.9.4)
breadboards: 1

parts:
  HC-SR04_Sensor_1 = HC-SR04 Ultrasonic Distance Sensor
  Part1 = Arduino Uno (Rev3)

nets:
  VCC: HC-SR04_Sensor_1.VCC, Part1.5V
  N1: HC-SR04_Sensor_1.TRIG, Part1.D11_PWM/MOSI
  N2: HC-SR04_Sensor_1.ECHO, Part1.D12/MISO
  GND: HC-SR04_Sensor_1.GND, Part1.GND
